# Fritzing sketch T.R.E.E.C.O (saved by Fritzing 0.9.5d)
circuit board: 16.1453cm x 11.361cm
breadboards: 1

parts:
  UPS_OUTPUT = 2.1mm Barrel Jack with Terminal Block
  S1 = SPST Switch [package=switch-spdt_lock.007s]
  Soil_Sensor = JXBS-3001-NPK-RS
  TTL_Converter = MAX485 Breakout [package=THT]
  12v_to_5v = RioRand LM2596
  ESP_32 = ESP32 DevKitc V4

nets:
  N1: UPS_OUTPUT.POS, S1.O
  N2: UPS_OUTPUT.NEG, 12v_to_5v.Pin_4
  N3: S1.S, Soil_Sensor.Pin_1, 12v_to_5v.Pin_3
  GND: Soil_Sensor.Pin_2, TTL_Converter.GND, 12v_to_5v.Pin_2, ESP_32.GND
  N4: Soil_Sensor.Pin_3, TTL_Converter.A
  N5: Soil_Sensor.Pin_4, TTL_Converter.B
  N6: TTL_Converter.RO, ESP_32.IO16
  N7: TTL_Converter.RE, ESP_32.IO4
  N8: TTL_Converter.DE, ESP_32.IO5
  N9: TTL_Converter.DI, ESP_32.IO17
  VCC: TTL_Converter.VCC, 12v_to_5v.Pin_1, ESP_32.5V

custom parts:
  JXBS-3001-NPK-RS: The NPK sensor is designed for detecting the content of nitrogen, phosphorus and potassium in soil, determining the fertility of the soil and facilitating the evaluation of the soil condition by the customer system.
  MAX485 Breakout: MAX485 RS485 breakout board
  ESP32 DevKitc V4: ESP32-DevKitC board with ESP32-WROOM-32 module. ESP32-DevKitC V4 is a small-sized ESP32-based development board produced by Espressif. Most of the pins on the ESP module are broken out to the pin headers on the board. The pins D0, D1, D2, D3, CMD and CLK are used internally for communication between ESP32 and SPI flash memory. They are grouped on both sides near the USB connector. Avoid using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
